# Fritzing sketch getMq3Val (saved by Fritzing 0.9.3b)
breadboards: 1

parts:
  U1 = NodeMCU V1.0
  Part1 = MQ-3 breakout
  LCM1602_IIC1 = LCM1602 IIC [part_number="LCM1602 IIC" chip_label="LCM1602 IIC" package="DIP (Dual Inline) [THT]"]
  LCD2 = LCD screen

nets:
  N1: U1.D1, LCM1602_IIC1.SCL
  N2: U1.D2, LCM1602_IIC1.SDA
  GND: U1.GND, Part1.GND, LCM1602_IIC1.GND
  VCC: U1.Vin, Part1.VCC, LCM1602_IIC1.VCC
  N3: U1.A0, Part1.AO
  VSS: LCM1602_IIC1.VSS, LCD2.VSS
  VDD: LCM1602_IIC1.VDD, LCD2.VDD
  N4: LCM1602_IIC1.V0, LCD2.V0
  N5: LCM1602_IIC1.RS, LCD2.RS
  N6: LCM1602_IIC1.RW, LCD2.R/W
  N7: LCM1602_IIC1.E, LCD2.E
  N8: LCM1602_IIC1.D0, LCD2.DB0
  N9: LCM1602_IIC1.D1, LCD2.DB1
  N10: LCM1602_IIC1.D2, LCD2.DB2
  N11: LCM1602_IIC1.D3, LCD2.DB3
  N12: LCM1602_IIC1.D4, LCD2.DB4
  N13: LCM1602_IIC1.D5, LCD2.DB5
  N14: LCM1602_IIC1.D6, LCD2.DB6
  N15: LCM1602_IIC1.D7, LCD2.DB7
  N16: LCM1602_IIC1.A, LCD2.LED+
  N17: LCM1602_IIC1.K, LCD2.LED-

custom parts:
  NodeMCU V1.0: ESP8266 based NodeMCU
  MQ-3 breakout: Alcohol sensor is capable of detecting alcohol (ethanol) particles on itself and gives the information in digital form back to us to manipulate with it. SKU:101251 • Voltage: 5V DC • Power: max 750mW • Measurement range: 0.04-4mg/L
  LCM1602 IIC: I2C-Module to use a 1602 or 2004 LCD on with the wire.h libory Serial LCD Modul
