# Fritzing sketch ignition (saved by Fritzing 0.9.3b)

parts:
  U1 = NodeMCU V1.0
  KY-1 = Keyes Relay [package=THT]
  Power_plug1 = Power plug
  S2 = Round Pushbutton
  M2 = DC Motor  # not connected

nets:
  N1: U1.3V3, KY-1.power
  N2: U1.GND, KY-1.ground
  N3: U1.D8, KY-1.signal
  N4: KY-1.NC, S2.leg0
  N5: KY-1.C, Power_plug1.VCC
  N6: Power_plug1.GND, S2.leg1

notes:
  car starter
  chuông báo động

custom parts:
  NodeMCU V1.0: ESP8266 based NodeMCU
  Keyes Relay: The Keyes 5V relay module is suitable for SCM development, home appliance control. It uses a 5V~12V TIL control signal which can control DC / AC signal.
